// Logisim project 15-02.circ as structural Verilog
module ADD_1 (
  input  A,
  input  B,
  input  VEM_1,
  output S,
  output VAL_1
);

  wire and_1_out, and_2_out, or_1_out, xor_1_out;

  xor xor_1 (xor_1_out, A, B);
  or or_1 (or_1_out, B, VEM_1);
  and and_1 (and_1_out, or_1_out, A);
  and and_2 (and_2_out, B, VEM_1);
  xor xor_2 (S, xor_1_out, VEM_1);
  or or_2 (VAL_1, and_1_out, and_2_out);
endmodule
